// Logisim project 微波炉.circ as structural Verilog: 9 circuits, main circuit main
module main (
  input  [15:0] in_1,
  input  in_2,
  input  [2:0] in_3,
  input  in_4,
  input  in_5
);

  wire clock_1_out, d_ff_1_q, \output , \写入 , \清屏 , \置零 , \解除锁定 ;
  wire [1:0] counter_1_q;
  wire [2:0] \状态机_1_out_2 ;
  wire [3:0] \启动_1_out_2 , \启动_1_out_3 , \启动_1_out_4 , \时停_1_out_6 , \时停_1_out_7 , \时停_1_out_8 ,
       \时停_1_out_9 , \设置时间_1_out_2 , \设置时间_1_out_3 ;
  wire [6:0] multiplexer_2_out, multiplexer_3_out;
  wire [7:0] \设置时间_1_out_5 ;
  wire [15:0] multiplexer_1_out, \烹饪_1_out_9 ;
  wire [15:12] \启动_1_time ;

  \启动  \u_启动_1  (.\time (\启动_1_time ), .out_2(\启动_1_out_2 ), .out_3(\启动_1_out_3 ), .out_4(\启动_1_out_4 ));
  Hex_Digit_Display hex_digit_display_1 (.value(\时停_1_out_9 ));  // open: dp
  Hex_Digit_Display hex_digit_display_2 (.value(\时停_1_out_6 ));  // open: dp
  Multiplexer #(.select(3), .width(16), .disabled("Z"), .enable("false")) multiplexer_1 (
    .in0({\启动_1_time , \启动_1_out_2 , \启动_1_out_3 , \启动_1_out_4 }),
    .in1({\设置时间_1_out_2 , \设置时间_1_out_3 , \设置时间_1_out_5 }), .in2(\烹饪_1_out_9 ), .in3(\烹饪_1_out_9 ),
    .in4(\烹饪_1_out_9 ), .out(multiplexer_1_out), .sel(\状态机_1_out_2 ));  // open: in5, in6, in7
  \烹饪  \u_烹饪_1  (
    .s2(in_1), .s3(\置零 ), .s4(in_4), .out_6(\烹饪_1_out_9 [15:12]), .out_7(\烹饪_1_out_9 [11:8]),
    .out_8(\烹饪_1_out_9 [7:4]), .out_9(\烹饪_1_out_9 [3:0]), .s5(in_2), .s1(\写入 ));
  \设置时间  \u_设置时间_1  (
    .out_2(\设置时间_1_out_2 ), .out_3(\设置时间_1_out_3 ), .out_4(\设置时间_1_out_5 [7:4]), .out_5(\设置时间_1_out_5 [3:0]),
    .in_1(in_1));
  Hex_Digit_Display hex_digit_display_3 (.value(\时停_1_out_7 ));  // open: dp
  Hex_Digit_Display hex_digit_display_4 (.value(\时停_1_out_8 ));  // open: dp
  \状态机  \u_状态机_1  (.in_1(in_3), .out_2(\状态机_1_out_2 ));
  \时停  \u_时停_1  (
    .output_2(\output ), .out_9(\时停_1_out_9 ), .out_6(\时停_1_out_6 ), .out_7(\时停_1_out_7 ),
    .out_8(\时停_1_out_8 ), .\解锁置零 (\解除锁定 ), .in_1(in_5), .\output (\output ), .in_5(multiplexer_1_out));
  Button button_1 (.out(\清屏 ));
  \输出done  \u_输出done_1  (.\烹饪中 (in_5), .in_2(multiplexer_1_out), .\output (\output ));
  Button button_2 (.out(\写入 ));
  Button button_3 (.out(\置零 ));
  Clock #(.highDuration(1), .lowDuration(1)) clock_1 (.out(clock_1_out));
  TTY #(.Char_bit_width(7), .rows(8), .cols(32), .trigger("rising")) tty_1 (
    .data(multiplexer_2_out), .clk(clock_1_out), .we(in_5), .clr(\清屏 ));
  Button button_4 (.out(\解除锁定 ));
  Counter #(.width(2), .max('h3), .ongoal("continue"), .trigger("rising"), .behavior("new")) counter_1 (
    .Q(counter_1_q), .clk(clock_1_out));  // open: load, D, count, carry, clr, preset, down
  D_Flip_Flop #(.trigger("rising"), .Pre_Clr_Positions("ABOVE_BELOW"), .NegatePresetClear("false"), .enable("false"), .NewFFLayout("true")) d_ff_1 (
    .clk(\output ), .D(1'b1), .Q(d_ff_1_q), .reset(\解除锁定 ));  // open: Qn, preset
  Multiplexer #(.select(1), .width(7), .disabled("Z"), .enable("false")) multiplexer_2 (
    .in0(7'b0100011), .in1(multiplexer_3_out), .out(multiplexer_2_out), .sel(d_ff_1_q));
  Multiplexer #(.select(2), .width(7), .disabled("Z"), .enable("false")) multiplexer_3 (
    .in0(7'b1000100), .in1(7'b1101111), .in2(7'b1101110), .in3(7'b1000101), .out(multiplexer_3_out),
    .sel(counter_1_q));

  // Other names for the same wires on the sheet: 写入使能 = in_2; 功能[2:0] = in_3; 时长[15:0] = in_1; 烹饪中 = in_5; 计时 = in_4

  // Notes on the sheet:
  //   功能表
  //   0：启动
  //   1：设置时间
  //   2：烹饪
  //   3：煎蛋
  //   4：热面包
  //   5：解冻
  //   :
  //   (烹饪时打开)
endmodule

module clock (
);

  wire button_1_out, clock_1_out, counter_1_carry, counter_3_carry, counter_5_carry, not_1_out, not_2_out,
       not_3_out, rev_p2;
  wire [3:0] counter_2_q, counter_3_q, counter_4_q, counter_5_q;

  Counter #(.width(8), .max('h3b), .ongoal("wrap"), .trigger("rising"), .behavior("new")) counter_1 (
    .carry(counter_1_carry), .clk(clock_1_out), .clr(button_1_out));  // open: load, D, count, Q, preset, down
  Counter #(.width(4), .max('h5), .ongoal("wrap"), .trigger("rising"), .behavior("new")) counter_2 (
    .Q(counter_2_q), .clk(not_1_out), .clr(button_1_out));  // open: load, D, count, carry, preset, down
  not not_1 (not_1_out, counter_3_carry);
  not not_2 (not_2_out, counter_1_carry);
  Counter #(.width(4), .max('h9), .ongoal("wrap"), .trigger("rising"), .behavior("new")) counter_3 (
    .Q(counter_3_q), .carry(counter_3_carry), .clk(not_2_out), .clr(button_1_out));  // open: load, D, count, preset, down
  Hex_Digit_Display hex_digit_display_1 (.value(counter_2_q));  // open: dp
  Hex_Digit_Display hex_digit_display_2 (.value(counter_3_q));  // open: dp
  Counter #(.width(4), .max('h5), .ongoal("wrap"), .trigger("rising"), .behavior("new")) counter_4 (
    .Q(counter_4_q), .clk(not_3_out), .clr(button_1_out), .down(rev_p2));  // open: load, D, count, carry, preset
  not not_3 (not_3_out, counter_5_carry);
  Hex_Digit_Display hex_digit_display_3 (.value(counter_5_q));  // open: dp
  Hex_Digit_Display hex_digit_display_4 (.value(counter_4_q));  // open: dp
  Clock #(.highDuration(1), .lowDuration(1)) clock_1 (.out(clock_1_out));
  // DipSwitch #(.NSwitches(1)) rev: pin names not known; wires that end beside it: counter_2_q, rev_p2
  // Probe on counter_5_carry
  Counter #(.width(4), .max('h9), .ongoal("wrap"), .trigger("rising"), .behavior("new")) counter_5 (
    .Q(counter_5_q), .carry(counter_5_carry), .clk(clock_1_out), .clr(button_1_out), .down(rev_p2));  // open: load, D, count, preset
  Button button_1 (.out(button_1_out));

  // Notes on the sheet:
  //   :
endmodule

module UI (
  input  in_1,
  input  in_2,
  input  in_3,
  input  in_4,
  input  in_5,
  input  [3:0] in_6,
  output out_7,
  output out_8,
  output [3:0] out_9,
  output out_10
);

  wire button_1_out, clock_1_out, clock_2_out, undriven, undriven_2;
  wire [3:0] counter_1_q;

  // D_Flip_Flop #(.trigger("latch"), .Pre_Clr_Positions("ABOVE_BELOW"), .NegatePresetClear("false"), .enable("false"), .NewFFLayout("true")) d_ff_1: pin names not known; wires that end beside it: in_1, in_2, out_7
  Clock #(.highDuration(1), .lowDuration(1)) clock_1 (.out(clock_1_out));
  Clock #(.highDuration(1), .lowDuration(1)) clock_2 (.out(clock_2_out));
  D_Flip_Flop #(.trigger("falling"), .Pre_Clr_Positions("ABOVE_BELOW"), .NegatePresetClear("false"), .enable("false"), .NewFFLayout("true")) d_ff_2 (
    .clk(clock_1_out), .D(undriven), .Q(out_8));  // open: Qn, preset, reset
  Counter #(.width(4), .max('h9), .ongoal("wrap"), .trigger("falling"), .behavior("new")) counter_1 (
    .Q(counter_1_q), .clk(out_10));  // open: load, D, count, carry, clr, preset, down
  Counter #(.width(4), .max('h9), .ongoal("wrap"), .trigger("falling"), .behavior("new")) counter_2 (
    .load(in_4), .D(in_6), .Q(out_9), .carry(out_10), .clk(clock_2_out), .clr(button_1_out));  // open: count, preset, down
  // OR_Gate or_1 has open pins: in0=undriven_2, out=open
  Hex_Digit_Display hex_digit_display_1 (.value(counter_1_q));  // open: dp
  Button button_1 (.out(button_1_out));
  Hex_Digit_Display hex_digit_display_2 (.value(out_9));  // open: dp
endmodule

// choice
module \状态机  (
  input  [2:0] in_1,
  output [2:0] out_2
);

  Multiplexer #(.select(3), .width(3), .disabled("Z"), .enable("false")) multiplexer_1 (
    .in0(3'b000), .in1(3'b001), .in2(3'b010), .in3(3'b011), .in4(3'b100), .in5(3'b101), .in6(3'b110),
    .in7(3'b111), .out(out_2), .sel(in_1));

  // Notes on the sheet:
  //   功能选择
endmodule

// 待机
module \启动  (
  output [3:0] \time ,
  output [3:0] out_2,
  output [3:0] out_3,
  output [3:0] out_4
);

  wire clock_1_out, counter_2_carry, counter_3_carry, not_1_out, not_2_out;

  Hex_Digit_Display hex_digit_display_1 (.value(4'b0001));  // open: dp
  Hex_Digit_Display hex_digit_display_2 (.value(4'b0101));  // open: dp
  Counter #(.width(4), .max('h5), .ongoal("wrap"), .trigger("rising"), .behavior("new")) counter_1 (
    .Q(out_3), .clk(not_1_out));  // open: load, D, count, carry, clr, preset, down
  not not_1 (not_1_out, counter_3_carry);
  Hex_Digit_Display hex_digit_display_3 (.value(out_3));  // open: dp
  Hex_Digit_Display hex_digit_display_4 (.value(out_4));  // open: dp
  Clock #(.highDuration(1), .lowDuration(1)) clock_1 (.out(clock_1_out));
  Counter #(.width(8), .max('h3b), .ongoal("wrap"), .trigger("rising"), .behavior("new")) counter_2 (
    .carry(counter_2_carry), .clk(clock_1_out));  // open: load, D, count, Q, clr, preset, down
  Counter #(.width(4), .max('h9), .ongoal("wrap"), .trigger("rising"), .behavior("new")) counter_3 (
    .Q(out_4), .carry(counter_3_carry), .clk(not_2_out));  // open: load, D, count, clr, preset, down
  not not_2 (not_2_out, counter_2_carry);
  // Probe on counter_3_carry

  assign out_2 = 4'b0101;
  assign \time  = 4'b0001;

  // Notes on the sheet:
  //   模拟系统时间
  //   小时
  //   :
  //   分钟进位
  //   秒
  //   分钟
endmodule

// 时长
module \设置时间  (
  input  [15:0] in_1,
  output [3:0] out_2,
  output [3:0] out_3,
  output [3:0] out_4,
  output [3:0] out_5
);

  Hex_Digit_Display hex_digit_display_1 (.value(in_1[11:8]));  // open: dp
  Hex_Digit_Display hex_digit_display_2 (.value(in_1[15:12]));  // open: dp
  Hex_Digit_Display hex_digit_display_3 (.value(in_1[7:4]));  // open: dp
  Hex_Digit_Display hex_digit_display_4 (.value(in_1[3:0]));  // open: dp

  assign out_2 = in_1[15:12];
  assign out_3 = in_1[11:8];
  assign out_4 = in_1[7:4];
  assign out_5 = in_1[3:0];

  // Notes on the sheet:
  //   将时长载入烹饪
  //   更新烹饪时间暂停计时
  //   输入时长
  //   :
  //   时钟
endmodule

module \烹饪  (
  input  s5,
  input  s1,
  input  s4,
  input  [15:0] s2,
  input  s3,
  output [3:0] out_6,
  output [3:0] out_7,
  output [3:0] out_8,
  output [3:0] out_9
);

  wire [4:0] counter_3_carry, multiplexer_1_out;
  wire [7:0] adder_1_out, bit_extender_1_out, bit_extender_2_out, multiplier_1_out;

  Multiplier #(.width(8)) multiplier_1 (.a(8'ha), .b(bit_extender_1_out), .out(multiplier_1_out));  // open: cin, cout
  assign bit_extender_1_out = {{4{1'b0}}, s2[7:4]};  // Bit_Extender bit_extender_1
  Multiplexer #(.select(1), .width(5), .disabled("Z"), .enable("false")) multiplexer_1 (
    .in0({{2{counter_3_carry[4]}}, counter_3_carry[2:0]}), .in1({5{1'b0}}), .out(multiplexer_1_out), .sel(s1));
  Adder #(.width(8)) adder_1 (.a(multiplier_1_out), .b(bit_extender_2_out), .out(adder_1_out));  // open: cin, cout
  // Probe on adder_1_out
  assign bit_extender_2_out = {{4{1'b0}}, s2[3:0]};  // Bit_Extender bit_extender_2
  Counter #(.width(8), .max('h3b), .ongoal("wrap"), .trigger("rising"), .behavior("new")) counter_1 (
    .load(s5), .D(adder_1_out), .count(s4), .carry(counter_3_carry[1]), .clk(multiplexer_1_out[3]), .clr(s3),
    .down(1'b1));  // open: Q, preset
  Counter #(.width(4), .max('h5), .ongoal("wrap"), .trigger("falling"), .behavior("new")) counter_2 (
    .load(s5), .D(s2[15:12]), .count(s4), .Q(out_6), .clk(multiplexer_1_out[0]), .clr(s3), .down(1'b1));  // open: carry, preset
  Counter #(.width(4), .max('h9), .ongoal("wrap"), .trigger("falling"), .behavior("new")) counter_3 (
    .load(s5), .D(s2[11:8]), .count(s4), .Q(out_7), .carry(counter_3_carry[0]), .clk(multiplexer_1_out[1]),
    .clr(s3), .down(1'b1));  // open: preset
  Hex_Digit_Display hex_digit_display_1 (.value(out_6));  // open: dp
  Hex_Digit_Display hex_digit_display_2 (.value(out_7));  // open: dp
  Counter #(.width(4), .max('h5), .ongoal("wrap"), .trigger("falling"), .behavior("new")) counter_4 (
    .load(s5), .D(s2[7:4]), .count(s4), .Q(out_8), .clk(multiplexer_1_out[2]), .clr(s3), .down(1'b1));  // open: carry, preset
  Hex_Digit_Display hex_digit_display_3 (.value(out_8));  // open: dp
  Hex_Digit_Display hex_digit_display_4 (.value(out_9));  // open: dp
  Clock #(.highDuration(1), .lowDuration(1)) clock_1 (.out(counter_3_carry[4]));
  Counter #(.width(4), .max('h9), .ongoal("wrap"), .trigger("rising"), .behavior("new")) counter_5 (
    .load(s5), .D(s2[3:0]), .count(s4), .Q(out_9), .carry(counter_3_carry[2]), .clk(multiplexer_1_out[4]),
    .clr(s3), .down(1'b1));  // open: preset

  // Notes on the sheet:
  //   同步秒模块
  //   写入
  //   写入使能
  //   分钟
  //   :
  //   置零
  //   秒
  //   同步所有计数器
  //   加载数据
  //   计时
  //   计数
endmodule

module \输出done  (
  input  \烹饪中 ,
  input  [15:0] in_2,
  output \output 
);

  wire comparator_1_eq;

  Comparator #(.width(16), .mode("twosComplement")) comparator_1 (
    .a({16{1'b0}}), .b(in_2), .eq(comparator_1_eq));  // open: gt, lt
  and and_1 (\output , \烹饪中 , comparator_1_eq);

  // Notes on the sheet:
  //   时钟信号
endmodule

module \时停  (
  input  in_1,
  input  \output ,
  input  output_2,
  input  \解锁置零 ,
  input  [15:0] in_5,
  output [3:0] out_6,
  output [3:0] out_7,
  output [3:0] out_8,
  output [3:0] out_9
);

  wire and_1_out, d_ff_1_q;

  D_Flip_Flop #(.trigger("rising"), .Pre_Clr_Positions("ABOVE_BELOW"), .NegatePresetClear("false"), .enable("false"), .NewFFLayout("true")) d_ff_1 (
    .clk(and_1_out), .D(output_2), .Q(d_ff_1_q), .reset(\解锁置零 ));  // open: Qn, preset
  Multiplexer #(.select(1), .width(16), .disabled("Z"), .enable("false")) multiplexer_1 (
    .in0(in_5), .in1({16{1'b0}}), .out({out_9, out_6, out_7, out_8}), .sel(d_ff_1_q));
  and and_1 (and_1_out, in_1, \output );

  // Notes on the sheet:
  //   烹饪中
  //   时钟
endmodule
